// Logisim project computer.circ as structural Verilog: 6 circuits, main circuit main
module main (
);

  wire mmap_1_dma, mmap_1_mem, pia_1_p5, pia_1_p6, pia_1_p7, pia_1_p8, pia_1_p9, pia_1_p10, pia_1_p11,
       pia_1_p12, pia_1_p13, pia_1_p17, the_dma_1_dclk;
  wire [1:0] pia_1_p4;
  wire [6:0] pia_1_p16;
  wire [7:0] matrix_driver_1_row0, matrix_driver_1_row1, matrix_driver_1_row2, matrix_driver_1_row3,
       matrix_driver_1_row4, matrix_driver_1_row5, matrix_driver_1_row6, matrix_driver_1_row7, pia_1_p14,
       pia_1_p15, the_dma_1_data;
  wire [7:7] pia_1_p16_2;
  wire [31:0] pia_1_p1, pia_1_p2, pia_1_p3;

  // pia pia_1: pin names not known; wires that end beside it: pia_1_p1, pia_1_p2, pia_1_p3, pia_1_p4, pia_1_p5, pia_1_p6, pia_1_p7, pia_1_p8, pia_1_p9, pia_1_p10, pia_1_p11, pia_1_p12, pia_1_p13, pia_1_p14, pia_1_p15, {pia_1_p16_2[7], pia_1_p16}, pia_1_p17
  cpu_5_stage_pipeline cpu_5_stage_pipeline_1 (
    .data_in(pia_1_p2), .rst(pia_1_p10), .clk(pia_1_p9), .hld(pia_1_p7), .mem_rd(pia_1_p6),
    .mem_wr(pia_1_p5), .data_out(pia_1_p3), .data_type(pia_1_p4), .addr(pia_1_p1), .hlda(pia_1_p8));
  Clock clock_1 (.out(pia_1_p9));
  mmap mmap_1 (.dma(mmap_1_dma), .mem(mmap_1_mem), .pia(pia_1_p11), .addr(pia_1_p1));
  the_dma the_dma_1 (
    .addr(pia_1_p1), .data(the_dma_1_data), .hld(pia_1_p7), .dclk(the_dma_1_dclk), .en(mmap_1_dma),
    .wr(pia_1_p5), .clk(pia_1_p9), .rst(pia_1_p10), .hlda(pia_1_p8), .cdata(pia_1_p3), .rs(pia_1_p1),
    .mdata(pia_1_p2));
  memory memory_1 (
    .data_out(pia_1_p2), .clk(pia_1_p9), .wr(pia_1_p5), .en(mmap_1_mem), .data_type(pia_1_p4),
    .data_in(pia_1_p3), .addr(pia_1_p1));
  Button RESET (.out(pia_1_p10));
  TTY #(.cols(24), .rows(6)) tty_1 (.data(pia_1_p15[6:0]), .clk(pia_1_p9), .we(pia_1_p12), .clr(pia_1_p10));
  DotMatrix #(.inputtype("row"), .matrixcols(8), .matrixrows(8)) dotmatrix_1 (
    .row0(matrix_driver_1_row0), .row1(matrix_driver_1_row1), .row2(matrix_driver_1_row2),
    .row3(matrix_driver_1_row3), .row4(matrix_driver_1_row4), .row5(matrix_driver_1_row5),
    .row6(matrix_driver_1_row6), .row7(matrix_driver_1_row7));
  matrix_driver matrix_driver_1 (
    .row1(matrix_driver_1_row1), .row2(matrix_driver_1_row2), .row3(matrix_driver_1_row3),
    .row4(matrix_driver_1_row4), .row5(matrix_driver_1_row5), .row6(matrix_driver_1_row6),
    .row0(matrix_driver_1_row0), .row7(matrix_driver_1_row7), .clk(the_dma_1_dclk), .rst(pia_1_p10),
    .data(the_dma_1_data));
  Keyboard keyboard_1 (.clk(pia_1_p9), .re(pia_1_p13), .clr(pia_1_p10), .avail(pia_1_p16_2[7]), .data(pia_1_p16));
  // Random #(.trigger("falling"), .width(3)) random_1: pin names not known; wires that end beside it: pia_1_p13, pia_1_p9, pia_1_p10
  Bit_Extender #(.in_width(3), .out_width(8), .\type ("zero")) bit_extender_1 (.out(pia_1_p14));  // open: in

  // Notes on the sheet:
  //   Rand Gen
  //   Type Here
endmodule

module memory (
  input  [31:0] addr,
  input  [1:0] data_type,
  input  clk,
  input  wr,
  input  en,
  input  [31:0] data_in,
  output [31:0] data_out
);

  wire and_1_out, not_1_out, or_1_out;
  wire [7:0] ram_1_p12, ram_1_p13, ram_1_p14, ram_1_p15;
  wire [19:0] bit_extender_1_out;

  or or_1 (or_1_out, data_type[0], data_type[1]);
  not not_1 (not_1_out, clk);
  Bit_Extender #(.in_width(32), .out_width(20), .\type ("zero")) bit_extender_1 (.in(addr), .out(bit_extender_1_out));
  and and_1 (and_1_out, wr, en);
  // RAM #(.addrWidth(20), .enables("line"), .line("quad"), .misaligned("true"), .\type ("nonvolatile")) ram_1: pin names not known; wires that end beside it: bit_extender_1_out, and_1_out, 1'b1, or_1_out, data_type[1], data_type[1], not_1_out, data_in[7:0], data_in[15:8], data_in[23:16], data_in[31:24], ram_1_p12, ram_1_p13, ram_1_p14, ram_1_p15
  assign data_out = en ? {ram_1_p15, ram_1_p14, ram_1_p13, ram_1_p12} : 32'bz;  // Controlled_Buffer controlled_buffer_1
endmodule

module mmap (
  input  [31:0] addr,
  output dma,
  output mem,
  output pia
);

  wire comparator_1_lt, comparator_2_eq, comparator_2_gt, comparator_3_eq, comparator_3_lt, comparator_4_eq,
       comparator_4_gt, comparator_5_eq, comparator_5_lt, or_1_out, or_2_out, or_3_out, or_4_out;
  wire [19:0] bit_extender_1_out;

  Comparator #(.mode("unsigned"), .width(32)) comparator_1 (
    .a(32'hffeff), .b(addr), .lt(comparator_1_lt));  // open: gt, eq
  Bit_Extender #(.in_width(32), .out_width(20), .\type ("zero")) bit_extender_1 (.in(addr), .out(bit_extender_1_out));
  Comparator #(.mode("unsigned"), .width(20)) comparator_2 (
    .a(bit_extender_1_out), .b(20'hffff0), .gt(comparator_2_gt), .eq(comparator_2_eq));  // open: lt
  Comparator #(.mode("unsigned"), .width(20)) comparator_3 (
    .a(bit_extender_1_out), .b(20'hffff7), .eq(comparator_3_eq), .lt(comparator_3_lt));  // open: gt
  Comparator #(.mode("unsigned"), .width(20)) comparator_4 (
    .a(bit_extender_1_out), .b(20'hffff8), .gt(comparator_4_gt), .eq(comparator_4_eq));  // open: lt
  Comparator #(.mode("unsigned"), .width(20)) comparator_5 (
    .a(bit_extender_1_out), .b(20'hffffa), .eq(comparator_5_eq), .lt(comparator_5_lt));  // open: gt
  or or_1 (or_1_out, comparator_5_lt, comparator_5_eq);
  or or_2 (or_2_out, comparator_4_eq, comparator_4_gt);
  and and_1 (dma, or_1_out, or_2_out, comparator_1_lt);
  nor nor_1 (mem, dma, pia);
  or or_3 (or_3_out, comparator_3_lt, comparator_3_eq);
  or or_4 (or_4_out, comparator_2_eq, comparator_2_gt);
  and and_2 (pia, comparator_1_lt, or_3_out, or_4_out);
endmodule

module input_port (
  input  I0,
  input  I1,
  input  I2,
  input  I3,
  input  I4,
  input  I5,
  input  I6,
  input  I7,
  output [7:0] data_out
);


  assign data_out = {I7, I6, I5, I4, I3, I2, I1, I0};
endmodule

module output_port (
  input  [7:0] data_in,
  output O0,
  output O1,
  output O2,
  output O3,
  output O4,
  output O5,
  output O6,
  output O7
);


  assign O0 = data_in[0];
  assign O1 = data_in[1];
  assign O2 = data_in[2];
  assign O3 = data_in[3];
  assign O4 = data_in[4];
  assign O5 = data_in[5];
  assign O6 = data_in[6];
  assign O7 = data_in[7];
endmodule

module matrix_driver (
  input  [7:0] data,
  input  clk,
  input  rst,
  output [7:0] row0,
  output [7:0] row1,
  output [7:0] row2,
  output [7:0] row3,
  output [7:0] row4,
  output [7:0] row5,
  output [7:0] row6,
  output [7:0] row7
);

  wire counter_1_carry, decoder_1_out0, decoder_1_out1, decoder_1_out2, decoder_1_out3, decoder_1_out4,
       decoder_1_out5, decoder_1_out6, decoder_1_out7;
  wire [2:0] counter_1_q;
  wire [7:0] register_1_q, register_2_q, register_3_q, register_4_q, register_5_q, register_6_q,
       register_7_q, register_8_q;

  Decoder #(.enable("false"), .select(3)) decoder_1 (
    .out0(decoder_1_out0), .out1(decoder_1_out1), .out2(decoder_1_out2), .out3(decoder_1_out3),
    .out4(decoder_1_out4), .out5(decoder_1_out5), .out6(decoder_1_out6), .out7(decoder_1_out7),
    .sel(counter_1_q));
  Counter #(.max('h7), .width(3)) counter_1 (
    .Q(counter_1_q), .carry(counter_1_carry), .clk(clk));  // open: load, D, count, up, clr
  Register register_1 (.D(data), .en(decoder_1_out0), .Q(register_1_q), .clk(clk), .clr(rst));
  Register register_2 (.D(data), .en(decoder_1_out1), .Q(register_2_q), .clk(clk), .clr(rst));
  Register register_3 (.D(data), .en(decoder_1_out2), .Q(register_3_q), .clk(clk), .clr(rst));
  Register register_4 (.D(data), .en(decoder_1_out3), .Q(register_4_q), .clk(clk), .clr(rst));
  Register register_5 (.D(data), .en(decoder_1_out4), .Q(register_5_q), .clk(clk), .clr(rst));
  Register register_6 (.D(data), .en(decoder_1_out5), .Q(register_6_q), .clk(clk), .clr(rst));
  Register register_7 (.D(data), .en(decoder_1_out6), .Q(register_7_q), .clk(clk), .clr(rst));
  Register register_8 (.D(data), .en(decoder_1_out7), .Q(register_8_q), .clk(clk), .clr(rst));
  Register #(.trigger("falling")) register_9 (
    .D(register_1_q), .Q(row0), .clk(counter_1_carry), .clr(rst));  // open: en
  Register #(.trigger("falling")) register_10 (
    .D(register_2_q), .Q(row1), .clk(counter_1_carry), .clr(rst));  // open: en
  Register #(.trigger("falling")) register_11 (
    .D(register_3_q), .Q(row2), .clk(counter_1_carry), .clr(rst));  // open: en
  Register #(.trigger("falling")) register_12 (
    .D(register_4_q), .Q(row3), .clk(counter_1_carry), .clr(rst));  // open: en
  Register #(.trigger("falling")) register_13 (
    .D(register_5_q), .Q(row4), .clk(counter_1_carry), .clr(rst));  // open: en
  Register #(.trigger("falling")) register_14 (
    .D(register_6_q), .Q(row5), .clk(counter_1_carry), .clr(rst));  // open: en
  Register #(.trigger("falling")) register_15 (
    .D(register_7_q), .Q(row6), .clk(counter_1_carry), .clr(rst));  // open: en
  Register #(.trigger("falling")) register_16 (
    .D(register_8_q), .Q(row7), .clk(counter_1_carry), .clr(rst));  // open: en
endmodule
